# Fritzing sketch RPI_Telecine-hole (1) (saved by Fritzing 0.9.4b)
circuit board: 6.50169cm x 5.6515cm
breadboards: 1

parts:
  LED1 = LED - 5mm [color="Red (633nm)" package="5 mm [THT]"]
  LED2 = LED - 5mm [color="Blue (525nm)" package="5 mm [THT]"]
  S2 = Pushbutton [package="[THT]"]
  R1 = Resistor [tolerance=±5% resistance=220 package=THT]
  R2 = Resistor [tolerance=±5% resistance=220 package=THT]
  C1 = Electrolytic Capacitor [capacitance=47µF package="100 mil [THT, electrolytic]"]
  Power_plug1 = Power plug
  J1 = screw terminal, 2 pins [part_number=LAMP]
  DRV_2 = Pololu DRV 8825 Stepper Motor Carrier, High Current [part_number=DRV8825 package=SO16]
  J2 = screw terminal, 4 pins [part_number=STEPPER]
  Q1 = npn-Powertransistor [part_number=TO220 package="TO220 [THT]"]
  S3 = Pushbutton [package="[THT]"]  # not connected
  J3 = Screw terminal - 2 pins [part_number=REED package=THT]
  J4 = double row female pin header, 40 pins [form="♀ (female)"]

nets:
  N1: LED1.cathode, R1.Pin_0
  N2: LED1.anode, S2.Pin_3, S2.Pin_4, J3.pin2, J4.pin38
  N3: LED2.cathode, R2.Pin_0
  N4: LED2.anode, J4.pin4
  N5: S2.Pin_1, S2.Pin_2, J3.pin1, J4.pin1
  N6: R1.Pin_1, R2.Pin_1, DRV_2.MS2, DRV_2.GND#8, J4.pin20
  N7: C1.-, Power_plug1.GND, DRV_2.GND#14, Q1.base
  N8: C1.+, Power_plug1.VCC, J1.pin1, DRV_2.VMOT
  N9: J1.pin2, Q1.emitter
  N10: DRV_2.MS1, J4.pin8
  N11: DRV_2.RESET, J4.pin36
  N12: DRV_2.SLEEP, J4.pin7
  N13: DRV_2.STEP, J4.pin6
  N14: DRV_2.DIR, J4.pin35
  N15: DRV_2.FAULT, J4.pin9
  N16: DRV_2.1B, J2.pin1
  N17: DRV_2.1A, J2.pin2
  N18: DRV_2.2A, J2.pin3
  N19: DRV_2.2B, J2.pin4
  N20: Q1.collector, J4.pin2

notes:
  LIGHT
  STEPPER
  12V DC
  REED

custom parts:
  Pololu DRV 8825 Stepper Motor Carrier, High Current: DRV 8825 This is a Stepper Motor Controller for integrated circuits. This breakout board for TI’s DRV8825 microstepping bipolar stepper motor driver features adjustable current limiting, over-current and over-temperature protection, and six microstep resolutions (down to 1/32-step). It operates from 8.2 V to 45 V and can deliver up to approximately 1.5 A per phase without a heat sink or forced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
