# Fritzing sketch RPI_Telecine (saved by Fritzing 0.9.3b)
circuit board: 8.53488cm x 5.63626cm
breadboards: 1

parts:
  LED1 = LED - 5mm [color="Red (633nm)" package="5 mm [THT]"]
  LED2 = LED - 5mm [color="Blue (525nm)" package="5 mm [THT]"]
  S2 = Pushbutton [package="[THT]"]
  R1 = Resistor [tolerance=±5% resistance=220 package=THT]
  R2 = Resistor [tolerance=±5% resistance=220 package=THT]
  Raspberry_Pi_1 = Raspberry Pi 3 [part_number=RPI-3-V1.2]
  C1 = Electrolytic Capacitor [capacitance=47µF package="100 mil [THT, electrolytic]"]
  Power_plug1 = Power plug
  J1 = screw terminal, 2 pins [part_number=LAMP]
  DRV_2 = Pololu DRV 8825 Stepper Motor Carrier, High Current [part_number=DRV8825 package=SO16]
  J2 = screw terminal, 4 pins [part_number=STEPPER]
  Q1 = npn-Powertransistor [part_number=TO220 package="TO220 [THT]"]
  S3 = Pushbutton [package="[THT]"]  # not connected
  J3 = Screw terminal - 2 pins [part_number=REED package=THT]

nets:
  N1: LED1.cathode, R1.Pin_0
  N2: LED1.anode, S2.Pin_3, S2.Pin_4, Raspberry_Pi_1.GPIO14, J3.pin2
  N3: LED2.cathode, R2.Pin_0
  N4: LED2.anode, Raspberry_Pi_1.GPIO4
  3V3: S2.Pin_1, S2.Pin_2, Raspberry_Pi_1.3v3, Raspberry_Pi_1.3V3, DRV_2.FAULT, J3.pin1
  N5: R1.Pin_1, R2.Pin_1, Raspberry_Pi_1.GND, DRV_2.MS2, DRV_2.GND#8
  N6: Raspberry_Pi_1.GPIO2, Q1.collector
  N7: Raspberry_Pi_1.GPIO17, DRV_2.STEP
  N8: Raspberry_Pi_1.GPIO27, DRV_2.SLEEP
  N9: Raspberry_Pi_1.GPIO22, DRV_2.MS1
  N10: Raspberry_Pi_1.GPIO18, DRV_2.DIR
  N11: Raspberry_Pi_1.GPIO15, DRV_2.RESET
  N12: C1.-, Power_plug1.GND, DRV_2.GND#14, Q1.base
  N13: C1.+, Power_plug1.VCC, J1.pin1, DRV_2.VMOT
  N14: J1.pin2, Q1.emitter
  N15: DRV_2.1B, J2.pin1
  N16: DRV_2.1A, J2.pin2
  N17: DRV_2.2A, J2.pin3
  N18: DRV_2.2B, J2.pin4

notes:
  LIGHT
  STEPPER
  12V DC
  REED

custom parts:
  Pololu DRV 8825 Stepper Motor Carrier, High Current: DRV 8825 This is a Stepper Motor Controller for integrated circuits. This breakout board for TI’s DRV8825 microstepping bipolar stepper motor driver features adjustable current limiting, over-current and over-temperature protection, and six microstep resolutions (down to 1/32-step). It operates from 8.2 V to 45 V and can deliver up to approximately 1.5 A per phase without a heat sink or forced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
